# Fritzing sketch Bootloading (saved by Fritzing 0.9.3b)
breadboards: 1

parts:
  U1 = atmega328 [package=dip]
  R1 = Resistor [tolerance=±5% resistance=10k package="2512 [SMD]"]
  R2 = Resistor [tolerance=±5% resistance=220 package="2512 [SMD]"]
  XTAL1 = Crystal [frequency="8 MHz" package=SMD]
  C2 = Ceramic Capacitor [capacitance=22pF package="0805 [SMD, multilayer]"]
  C3 = Ceramic Capacitor [capacitance=22pF package="0805 [SMD, multilayer]"]
  LED1 = LED - 5mm [color="Red (633nm)" package="5 mm [THT]"]
  Part1 = Arduino Uno (Rev3)

nets:
  N1: U1.RESET, R1.Pin_0
  VCC: U1.VCC, U1.AVCC, R1.Pin_1, Part1.5V
  GND: U1.GND, C2.1, C3.1, LED1.anode, Part1.GND
  N2: U1.XLAT1, XTAL1.pin_0, C2.0
  N3: U1.XLAT2, XTAL1.pin_1, C3.0
  N4: U1.D10_(PWM), Part1.RESET
  N5: U1.D11_(PWM), Part1.D11_PWM/MOSI
  N6: U1.D12, Part1.D12/MISO
  N7: U1.D13, R2.Pin_0, Part1.D13/SCK
  N8: R2.Pin_1, LED1.cathode
